# Fritzing sketch board (saved by Fritzing 0.9.3b)
circuit board: 8.46667cm x 5.64444cm
breadboards: 1

parts:
  Часть1 = Arduino Nano (Rev3.0)
  TSOP_1739 = TSOP312.., 314.. [part_number="TSOP 1738" package=THT]
  LED1 = LEDs [package=led10mm]

nets:
  N1: Часть1.GND, TSOP_1739.Vs, LED1.A
  N2: Часть1.D2, TSOP_1739.GND
  N3: Часть1.D3, LED1.C
  N4: Часть1.3V3, TSOP_1739.Data
